# Fritzing sketch example-motorized(relays)-v1 (saved by Fritzing 0.9.9b)
breadboards: 1

parts:
  WeMos_D1_Mini1 = WeMos D1 Mini  # not connected
  Power_plug1 = Power plug
  J1 = JST-B3P-VH [part_number=JST-B3P-VH package=THT]
  WeMos_D1_Mini_Relay_Shield_V1 = WeMos D1 Mini Relay Shield V2
  WeMos_D1_Mini_Relay_Shield_V2 = WeMos D1 Mini Relay Shield V2

nets:
  N1: Power_plug1.GND, J1.pin2
  N2: Power_plug1.VCC, WeMos_D1_Mini_Relay_Shield_V1.COM
  N3: J1.pin1, WeMos_D1_Mini_Relay_Shield_V2.NC
  N4: J1.pin3, WeMos_D1_Mini_Relay_Shield_V2.NO
  N5: WeMos_D1_Mini_Relay_Shield_V1.NO, WeMos_D1_Mini_Relay_Shield_V2.COM

notes:
  OPEN
  GND
  CLOSE
