# Fritzing sketch example-solenoid_sketch (saved by Fritzing 0.9.9b)
breadboards: 1

parts:
  WeMos_D1_Mini_Relay_Shield_V1 = WeMos D1 Mini Relay Shield V2
  WeMos_D1_Mini1 = WeMos D1 Mini  # not connected
  VALVE1 = Plastic Solenoid Valve
  Power_plug1 = Power plug

nets:
  N1: WeMos_D1_Mini_Relay_Shield_V1.COM, Power_plug1.GND
  N2: WeMos_D1_Mini_Relay_Shield_V1.NO, VALVE1.no_name_yet#2
  N3: VALVE1.no_name_yet#1, Power_plug1.VCC
